# Fritzing sketch alyrp-leonardo-i2c (saved by Fritzing 0.9.3b)

parts:
  Componente1 = Arduino Leonardo (Rev3b)
  Componente2 = MicroSD Card Module
  U2 = LCD-16X2 [package=lcd-16x2]

nets:
  N1: Componente1.D2/SDA, U2.VDD
  N2: Componente1.D3_PWM/SCL, U2.VSS
  N3: Componente1.5V, U2.VO
  GND: Componente1.GND, Componente2.GND, U2.RS
  N4: Componente1.D10_PWM/A10, Componente2.CS
